# Fritzing sketch FinalWiringDiagram_OSUART4201_PaviaAndLendzian (saved by Fritzing 0.9.4)
breadboards: 2

parts:
  U1 = ESP32-38PinWide [part_number=ESP32-38PinWide]
  KY-1 = Keyes Relay [package=THT]
  M1 = DC Motor
  D2F1 = D2F-FL Omron Snap Action Limit Switch with Level
  PS1 = prefix0000 [part_number=S-350-60]
  NEOPIXEL1 = Neopixel Strip -- Black (60/m) [part_number=1461]
  LCD1 = LCD screen
  R1 = Rotary Potentiometer (Small) [maximum_resistance=100kΩ package=THT]
  DFRobot_DFPlayer_Mini1 = DFRobot DFPlayer Mini [part_number=DFR0299]
  SPKR1 = Loudspeaker
  R2 = Rotary Potentiometer (Small) [maximum_resistance=100kΩ package=THT]
  R3 = Rotary Potentiometer (Small) [maximum_resistance=100kΩ package=THT]
  JACK1 = 2.1mm Barrel Jack with Terminal Block

nets:
  N1: U1.GPIO34, R3.wiper
  N2: U1.GPIO32, KY-1.signal
  N3: U1.GPIO25, DFRobot_DFPlayer_Mini1.RX
  N4: U1.GPIO26, DFRobot_DFPlayer_Mini1.TX
  N5: U1.GPIO14, R2.wiper
  N6: U1.GPIO12, D2F1.NO
  GND: U1.GPIO11, KY-1.ground, D2F1.COM, PS1.connector3, NEOPIXEL1.GND, LCD1.VSS, LCD1.R/W, LCD1.LED-, R1.leg2, DFRobot_DFPlayer_Mini1.GND-1, DFRobot_DFPlayer_Mini1.GND-2, R2.leg2, R3.leg1
  VIN: U1.VIN, KY-1.power, PS1.connector2, NEOPIXEL1.+5V, LCD1.VDD, LCD1.LED+, R1.leg1, DFRobot_DFPlayer_Mini1.VCC, R2.leg1, R3.leg2
  N7: U1.GPIO15, LCD1.DB7
  N8: U1.GPIO16, LCD1.DB6
  N9: U1.GPIO17, LCD1.DB5
  N10: U1.GPIO5, NEOPIXEL1.DI
  N11: U1.GPIO18, LCD1.DB4
  N12: U1.GPIO19, LCD1.RS
  N13: U1.GPIO23, LCD1.E
  N14: KY-1.C, JACK1.NEG
  N15: KY-1.NO, M1.pin_2
  N16: M1.pin_1, JACK1.POS
  N17: LCD1.V0, R1.wiper
  N18: DFRobot_DFPlayer_Mini1.SPK_1, SPKR1.pin2
  N19: DFRobot_DFPlayer_Mini1.SPK_2, SPKR1.pin1

notes:
  Board shown has some pins in different positions than the physical board, so wiring in this diagram will be based on the labels on the pins rather than their physical positions.
  NO
  (Normally Open)
  COM
  (Common Ground)
  AC to 5V DC Power

custom parts:
  ESP32-38PinWide: Generic 38-Pin ESP32 with wide format (only access to one side of pins on a breadboard) based on Stephen Lilley's HiLetgo ESP-WROOM-32 ESP32 ESP-32S Development Board.
  Keyes Relay: The Keyes 5V relay module is suitable for SCM development, home appliance control. It uses a 5V~12V TIL control signal which can control DC / AC signal.
  D2F-FL Omron Snap Action Limit Switch with Level: Snap action switch with stainless steel lever.
  Neopixel Strip -- Black (60/m): Neopixel Strip, Black, 60 pixels per meter.
